// Digital circuit CPU.dig as structural Verilog
module CPU (
  input  Op0,
  input  Op1,
  input  Op2
);

  wire acumulator_1_s0, acumulator_1_s1, acumulator_1_s2, acumulator_1_s3, acumulator_1_s4, acumulator_1_s5,
       acumulator_1_s6, acumulator_1_s7, Ad, Clk, Clr, Cp, Ea, Ep, instruction_register_1_c0,
       memory_address_register_1_s0, memory_address_register_1_s1, memory_address_register_1_s2,
       memory_address_register_1_s3, memory_address_register_1_s4, memory_address_register_1_s5,
       memory_address_register_1_s6, memory_address_register_1_s7, NCE, NEi, NLa, NLb, NLi, NLm, NLo,
       ram_1_s0, ram_1_s1, ram_1_s2, ram_1_s3, ram_1_s4, ram_1_s5, ram_1_s6, ram_1_s7, register_b_1_s0,
       register_b_1_s1, register_b_1_s2, register_b_1_s3, register_b_1_s4, register_b_1_s5, register_b_1_s6,
       register_b_1_s7, ring_counter_1_q0, ring_counter_1_q1, ring_counter_1_q2, ula_1_eq, ula_1_out_20,
       ula_1_plus;
  wire [3:0] register_out_1_s0, register_out_1_s4;

  PullDown pulldown_1 (.out(Cp));
  PullDown pulldown_2 (.out(Ep));
  PullDown pulldown_3 (.out(Clr));
  PullDown pulldown_4 (.out(Clk));
  Ring_Counter ring_counter_1 (
    .Clk(Clk), .Clr(Clr), .Q0(ring_counter_1_q0), .Q1(ring_counter_1_q1), .Q2(ring_counter_1_q2), .Q3(Ea));  // open: Q4, Q5
  DiodeForward diodeforward_1 (.in(ring_counter_1_q0), .out(Ep));
  DiodeForward diodeforward_2 (.in(ring_counter_1_q1), .out(Cp));
  PullDown pulldown_5 (.out(Clk));
  PullDown pulldown_6 (.out(NLm));
  DiodeForward diodeforward_3 (.in(ring_counter_1_q1), .out(NLm));
  DiodeForward diodeforward_4 (.in(ring_counter_1_q2), .out(NLm));
  PullDown pulldown_7 (.out(NCE));
  PullDown pulldown_8 (.out(Clr));
  PullDown pulldown_9 (.out(Clk));
  PullDown pulldown_10 (.out(Ad));
  DiodeForward diodeforward_5 (.in(ring_counter_1_q0), .out(NCE));
  DiodeForward diodeforward_6 (.in(ring_counter_1_q0), .out(Ad));
  DiodeForward diodeforward_7 (.in(ring_counter_1_q1), .out(NCE));
  DiodeForward diodeforward_8 (.in(ring_counter_1_q1), .out(Ad));
  PullDown pulldown_11 (.out(NLi));
  PullDown pulldown_12 (.out(Clk));
  PullDown pulldown_13 (.out(Clr));
  PullDown pulldown_14 (.out(NEi));
  DiodeForward diodeforward_9 (.in(ring_counter_1_q0), .out(NLi));
  DiodeForward diodeforward_10 (.in(ring_counter_1_q0), .out(NEi));
  DiodeForward diodeforward_11 (.in(ring_counter_1_q1), .out(NLi));
  DiodeForward diodeforward_12 (.in(ring_counter_1_q1), .out(NEi));
  DiodeForward diodeforward_13 (.in(ring_counter_1_q2), .out(NEi));
  RAM ram_1 (
    .I0(memory_address_register_1_s0), .I1(memory_address_register_1_s1), .I2(memory_address_register_1_s2),
    .I3(memory_address_register_1_s3), .I4(memory_address_register_1_s4), .I5(memory_address_register_1_s5),
    .I6(memory_address_register_1_s6), .I7(memory_address_register_1_s7), .NCe(NCE), .Clr(Clr), .Clk(Clk),
    .A(memory_address_register_1_s0), .B(memory_address_register_1_s1), .C(memory_address_register_1_s2),
    .Ad(Ad), .S0(ram_1_s0), .S1(ram_1_s1), .S2(ram_1_s2), .S3(ram_1_s3), .S4(ram_1_s4), .S5(ram_1_s5),
    .S6(ram_1_s6), .S7(ram_1_s7));
  Instruction_Register instruction_register_1 (
    .NEi(NEi), .Clr(Clr), .Clk(Clk), .NLi(NLi), .I0(ram_1_s0), .I1(ram_1_s1), .I2(ram_1_s2), .I3(ram_1_s3),
    .I4(ram_1_s4), .I5(ram_1_s5), .I6(ram_1_s6), .I7(ram_1_s7), .C0(instruction_register_1_c0),
    .C1(instruction_register_1_c0), .C2(instruction_register_1_c0), .C3(instruction_register_1_c0),
    .Op0(ram_1_s4), .Op1(ram_1_s5), .Op2(ram_1_s6), .Op3(ram_1_s7));
  Program_Counter program_counter_1 (
    .Cp(Cp), .Ep(Ep), .Clr(Clr), .NClk(Clk), .S0(ram_1_s0), .S1(ram_1_s1), .S2(ram_1_s2), .S3(ram_1_s3));
  Memory_Address_Register memory_address_register_1 (
    .NLm(NLm), .Clk(Clk), .I0(ram_1_s0), .I1(ram_1_s1), .I2(ram_1_s2), .I3(ram_1_s3), .I4(ram_1_s4),
    .I5(ram_1_s5), .I6(ram_1_s6), .I7(ram_1_s7), .S0(memory_address_register_1_s0),
    .S1(memory_address_register_1_s1), .S2(memory_address_register_1_s2), .S3(memory_address_register_1_s3),
    .S4(memory_address_register_1_s4), .S5(memory_address_register_1_s5), .S6(memory_address_register_1_s6),
    .S7(memory_address_register_1_s7));
  Register_B register_b_1 (
    .NLb(NLb), .Clk(Clk), .I0(ram_1_s0), .I1(ram_1_s1), .I2(ram_1_s2), .I3(ram_1_s3), .I4(ram_1_s4),
    .I5(ram_1_s5), .I6(ram_1_s6), .I7(ram_1_s7), .S0(register_b_1_s0), .S1(register_b_1_s1),
    .S2(register_b_1_s2), .S3(register_b_1_s3), .S4(register_b_1_s4), .S5(register_b_1_s5),
    .S6(register_b_1_s6), .S7(register_b_1_s7));
  Register_OUT register_out_1 (
    .NLo(NLo), .Clk(Clk), .I0(ram_1_s0), .I1(ram_1_s1), .I2(ram_1_s2), .I3(ram_1_s3), .I4(ram_1_s4),
    .I5(ram_1_s5), .I6(ram_1_s6), .I7(ram_1_s7), .S0(register_out_1_s0[0]), .S1(register_out_1_s0[1]),
    .S2(register_out_1_s0[2]), .S3(register_out_1_s0[3]), .S4(register_out_1_s4[0]),
    .S5(register_out_1_s4[1]), .S6(register_out_1_s4[2]), .S7(register_out_1_s4[3]));
  Button u_Clk (.out(Clk));
  Button u_Clr (.out(Clr));
  Acumulator acumulator_1 (
    .NLa(NLa), .Ea(Ea), .Clk(Clk), .I0(ram_1_s0), .I1(ram_1_s1), .I2(ram_1_s2), .I3(ram_1_s3), .I4(ram_1_s4),
    .I5(ram_1_s5), .I6(ram_1_s6), .I7(ram_1_s7), .S0(acumulator_1_s0), .S1(acumulator_1_s1),
    .S2(acumulator_1_s2), .S3(acumulator_1_s3), .S4(acumulator_1_s4), .S5(acumulator_1_s5),
    .S6(acumulator_1_s6), .S7(acumulator_1_s7));
  Seven_Seg_Hex seven_seg_hex_1 (.d(register_out_1_s4), .dp(1'b0));
  Seven_Seg_Hex seven_seg_hex_2 (.d(register_out_1_s0), .dp(1'b0));
  ULA ula_1 (
    .A0(acumulator_1_s0), .B0(register_b_1_s0), .A1(acumulator_1_s1), .B1(register_b_1_s1),
    .A2(acumulator_1_s2), .B2(register_b_1_s2), .A3(acumulator_1_s3), .B3(register_b_1_s3),
    .A4(acumulator_1_s4), .B4(register_b_1_s4), .A5(acumulator_1_s5), .B5(register_b_1_s5),
    .A6(acumulator_1_s6), .B6(register_b_1_s6), .A7(acumulator_1_s7), .B7(register_b_1_s7), .C0(Op0),
    .C1(Op1), .C2(Op2), .Eu(Ea), .out_20(ula_1_out_20), .eq(ula_1_eq), .plus(ula_1_plus), .S0(ram_1_s0),
    .S1(ram_1_s1), .S2(ram_1_s2), .S3(ram_1_s3), .S4(ram_1_s4), .S5(ram_1_s5), .S6(ram_1_s6), .S7(ram_1_s7));
  LED plus (.in(ula_1_plus));
  LED led (.in(ula_1_out_20));
  LED eq (.in(ula_1_eq));
  DiodeForward diodeforward_14 (.in(ring_counter_1_q1), .out(NLo));
  DiodeForward diodeforward_15 (.in(ring_counter_1_q2), .out(NLo));
  PullDown pulldown_15 (.out(NLo));
  PullDown pulldown_16 (.out(Clk));
  DiodeForward diodeforward_16 (.in(ring_counter_1_q0), .out(NLo));
  DiodeForward diodeforward_17 (.in(ring_counter_1_q0), .out(NLb));
  DiodeForward diodeforward_18 (.in(ring_counter_1_q1), .out(NLb));
  DiodeForward diodeforward_19 (.in(ring_counter_1_q2), .out(NLb));
  PullDown pulldown_17 (.out(NLb));
  PullDown pulldown_18 (.out(Clk));
  DiodeForward diodeforward_20 (.in(ring_counter_1_q0), .out(NLa));
  DiodeForward diodeforward_21 (.in(ring_counter_1_q1), .out(NLa));
  DiodeForward diodeforward_22 (.in(ring_counter_1_q2), .out(NLa));
  PullDown pulldown_19 (.out(NLa));
  PullDown pulldown_20 (.out(Ea));
  PullDown pulldown_21 (.out(Clk));
  // also tied to GND on the sheet: instruction_register_1_c0

  // Other names for the same wires on the sheet: Eu = Ea

  // Notes on the sheet:
  //   FETCH:
  //   T2:
  //   Cp Ep NLm NCE Ad  NLi NEi NLa Ea  Eu NLb NLa
  //   1    0     1     1    1     1   1     1    0   0    1     1
  //   T1:
  //   Cp Ep NLm NCE Ad  NLi NEi NLa Ea  Eu NLb NLa
  //   1    0     1     1    1     1   1     1    0   0    1     1
  //   T0:
  //   Cp Ep NLm NCE Ad  NLi NEi NLa Ea  Eu NLb NLa
  //   0    1     0     1    1     1   1     1    0   0    1     1
endmodule
