// Digital circuit Instruction Register.dig as structural Verilog
module Instruction_Register (
  input  NEi,
  input  Clr,
  input  Clk,
  input  NLi,
  input  I0,
  input  I1,
  input  I2,
  input  I3,
  input  I4,
  input  I5,
  input  I6,
  input  I7,
  output C0,
  output C1,
  output C2,
  output C3,
  output Op0,
  output Op1,
  output Op2,
  output Op3
);

  wire not_1_out, not_2_out;

  not not_1 (not_1_out, NEi);
  not not_2 (not_2_out, NLi);
  Register register_1 (
    .Clk(Clk), .Read(not_1_out), .D0(I0), .Write(not_2_out), .Clr(Clr), .D1(I1), .D2(I2), .D3(I3), .D4(I4),
    .D5(I5), .D6(I6), .D7(I7), .Q0(Op0), .Q1(Op1), .Q2(Op2), .Q3(Op3), .Q4(C0), .Q5(C1), .Q6(C2), .Q7(C3));
endmodule
