// Digital circuit Memory Address Register.dig as structural Verilog
module Memory_Address_Register (
  input  NLm,
  input  Clk,
  input  I0,
  input  I1,
  input  I2,
  input  I3,
  input  I4,
  input  I5,
  input  I6,
  input  I7,
  output S0,
  output S1,
  output S2,
  output S3,
  output S4,
  output S5,
  output S6,
  output S7
);

  wire not_1_out;

  not not_1 (not_1_out, NLm);
  Register register_1 (
    .Clk(Clk), .Read(1'b1), .D0(I0), .Write(not_1_out), .Clr(1'b0), .D1(I1), .D2(I2), .D3(I3), .D4(I4),
    .D5(I5), .D6(I6), .D7(I7), .Q0(S0), .Q1(S1), .Q2(S2), .Q3(S3), .Q4(S4), .Q5(S5), .Q6(S6), .Q7(S7));
endmodule
