// Digital circuit Program Counter.dig as structural Verilog
module Program_Counter (
  input  Cp,
  input  Ep,
  input  NClr,
  input  NClk,
  output S0,
  output S1,
  output S2,
  output S3,
  output S4,
  output S5,
  output S6,
  output S7
);

  wire adder_1_s0, adder_1_s1, adder_1_s2, adder_1_s3, adder_1_s4, adder_1_s5, adder_1_s6, adder_1_s7,
       not_1_out, not_2_out;

  not not_1 (not_1_out, NClk);
  not not_2 (not_2_out, NClr);
  Adder adder_1 (
    .A0(S0), .B0(Cp), .A1(S1), .B1(1'b0), .A2(S2), .B2(1'b0), .A3(S3), .B3(1'b0), .A4(S4), .B4(1'b0),
    .A5(S5), .B5(1'b0), .A6(S6), .B6(1'b0), .A7(S7), .B7(1'b0), .S0(adder_1_s0), .S1(adder_1_s1),
    .S2(adder_1_s2), .S3(adder_1_s3), .S4(adder_1_s4), .S5(adder_1_s5), .S6(adder_1_s6), .S7(adder_1_s7));  // open: Ov
  Register register_1 (
    .Clk(not_1_out), .Read(Ep), .D0(adder_1_s0), .Write(Cp), .Clr(not_2_out), .D1(adder_1_s1),
    .D2(adder_1_s2), .D3(adder_1_s3), .D4(adder_1_s4), .D5(adder_1_s5), .D6(adder_1_s6), .D7(adder_1_s7),
    .Q0(S0), .Q1(S1), .Q2(S2), .Q3(S3), .Q4(S4), .Q5(S5), .Q6(S6), .Q7(S7));
endmodule
