// Digital circuit Register.dig as structural Verilog
module Register (
  input  Clk,
  input  Read,
  input  D0,
  input  Write,
  input  Clr,
  input  D1,
  input  D2,
  input  D3,
  input  D4,
  input  D5,
  input  D6,
  input  D7,
  output Q0,
  output Q1,
  output Q2,
  output Q3,
  output Q4,
  output Q5,
  output Q6,
  output Q7
);

  wire d_ff_as_1_q, d_ff_as_2_q, d_ff_as_3_q, d_ff_as_4_q, d_ff_as_5_q, d_ff_as_6_q, d_ff_as_7_q,
       d_ff_as_8_q, driver_1_out, driver_2_out, driver_3_out, driver_4_out, driver_5_out, driver_6_out,
       driver_7_out, driver_8_out, driver_9_out, driver_10_out, driver_11_out, driver_12_out, driver_13_out,
       driver_14_out, driver_15_out, driver_16_out;

  assign driver_1_out = Write ? Clk : 1'bz;  // Driver driver_1
  D_FF_AS d_ff_as_1 (.Set(1'b0), .D(D7), .C(driver_1_out), .Clr(Clr), .Q(d_ff_as_1_q));  // open: nQ
  assign driver_2_out = Read ? d_ff_as_1_q : 1'bz;  // Driver driver_2
  PullDown pulldown_1 (.out(Q7));
  DiodeForward diodeforward_1 (.in(driver_2_out), .out(Q7));
  assign driver_3_out = Write ? Clk : 1'bz;  // Driver driver_3
  D_FF_AS d_ff_as_2 (.Set(1'b0), .D(D6), .C(driver_3_out), .Clr(Clr), .Q(d_ff_as_2_q));  // open: nQ
  assign driver_4_out = Read ? d_ff_as_2_q : 1'bz;  // Driver driver_4
  PullDown pulldown_2 (.out(Q6));
  DiodeForward diodeforward_2 (.in(driver_4_out), .out(Q6));
  assign driver_5_out = Write ? Clk : 1'bz;  // Driver driver_5
  D_FF_AS d_ff_as_3 (.Set(1'b0), .D(D5), .C(driver_5_out), .Clr(Clr), .Q(d_ff_as_3_q));  // open: nQ
  PullDown pulldown_3 (.out(Q5));
  DiodeForward diodeforward_3 (.in(driver_6_out), .out(Q5));
  assign driver_6_out = Read ? d_ff_as_3_q : 1'bz;  // Driver driver_6
  assign driver_7_out = Write ? Clk : 1'bz;  // Driver driver_7
  D_FF_AS d_ff_as_4 (.Set(1'b0), .D(D4), .C(driver_7_out), .Clr(Clr), .Q(d_ff_as_4_q));  // open: nQ
  PullDown pulldown_4 (.out(Q4));
  DiodeForward diodeforward_4 (.in(driver_8_out), .out(Q4));
  assign driver_8_out = Read ? d_ff_as_4_q : 1'bz;  // Driver driver_8
  assign driver_9_out = Write ? Clk : 1'bz;  // Driver driver_9
  D_FF_AS d_ff_as_5 (.Set(1'b0), .D(D3), .C(driver_9_out), .Clr(Clr), .Q(d_ff_as_5_q));  // open: nQ
  assign driver_10_out = Read ? d_ff_as_5_q : 1'bz;  // Driver driver_10
  PullDown pulldown_5 (.out(Q3));
  DiodeForward diodeforward_5 (.in(driver_10_out), .out(Q3));
  assign driver_11_out = Write ? Clk : 1'bz;  // Driver driver_11
  D_FF_AS d_ff_as_6 (.Set(1'b0), .D(D2), .C(driver_11_out), .Clr(Clr), .Q(d_ff_as_6_q));  // open: nQ
  assign driver_12_out = Read ? d_ff_as_6_q : 1'bz;  // Driver driver_12
  PullDown pulldown_6 (.out(Q2));
  DiodeForward diodeforward_6 (.in(driver_12_out), .out(Q2));
  assign driver_13_out = Write ? Clk : 1'bz;  // Driver driver_13
  D_FF_AS d_ff_as_7 (.Set(1'b0), .D(D1), .C(driver_13_out), .Clr(Clr), .Q(d_ff_as_7_q));  // open: nQ
  PullDown pulldown_7 (.out(Q1));
  DiodeForward diodeforward_7 (.in(driver_14_out), .out(Q1));
  assign driver_14_out = Read ? d_ff_as_7_q : 1'bz;  // Driver driver_14
  assign driver_15_out = Write ? Clk : 1'bz;  // Driver driver_15
  D_FF_AS d_ff_as_8 (.Set(1'b0), .D(D0), .C(driver_15_out), .Clr(Clr), .Q(d_ff_as_8_q));  // open: nQ
  PullDown pulldown_8 (.out(Q0));
  DiodeForward diodeforward_8 (.in(driver_16_out), .out(Q0));
  assign driver_16_out = Read ? d_ff_as_8_q : 1'bz;  // Driver driver_16
endmodule
