// Digital circuit Selector.dig as structural Verilog
module Selector (
  input  A,
  input  B,
  input  C,
  output S0,
  output S1,
  output S2,
  output S3,
  output S4,
  output S5
);

  wire not_1_out, not_2_out, not_3_out;

  not not_1 (not_1_out, C);
  not not_2 (not_2_out, B);
  not not_3 (not_3_out, A);
  and and_1 (S0, not_3_out, not_2_out, not_1_out);
  and and_2 (S1, A, not_2_out, not_1_out);
  and and_3 (S2, not_3_out, B, not_1_out);
  and and_4 (S3, A, B, not_1_out);
  and and_5 (S4, C, not_3_out, not_2_out);
  and and_6 (S5, A, not_2_out, C);

  // Notes on the sheet:
  //   000
  //   001
  //   010
  //   011
  //   100
  //   101
endmodule
